// Digital circuit signal generator and character indexer.dig as structural Verilog
module signal_generator_and_character_indexer (
  input  pxl
);

  wire _7400_1_pin4, _7400_1_pin5, _7400_1_pin6, _7404_2_pin8, _7404_2_pin10, _7404_2_pin12, _7420_1_pin6,
       _7458_1_pin1, _7458_1_pin3, _7458_1_pin4, _7458_1_pin5, _7458_1_pin8, _7458_1_pin12, _7458_1_pin13,
       _7458_2_pin6, _7458_2_pin8, _74161_1_pin1, _74161_1_pin15, _74161_2_pin15, _74161_4_pin15,
       _74161_5_pin15, _744075_1_pin3, _744075_1_pin4, _744075_1_pin6, _744075_1_pin8, _744075_1_pin9,
       _744075_1_pin10, _744075_1_pin13, _744075_2_pin9, not_1_out;
  wire [6:0] _7420_1_pin4;
  wire [7:0] charBuf_d, charGen_d;
  wire [14:0] _7420_1_pin2;

  _74161 _74161_1 (
    .pin1(_74161_1_pin1), .pin2(pxl), .pin3(1'b0), .pin4(1'b0), .pin5(1'b0), .pin6(1'b0), .pin7(1'b1),
    .pin8(1'b0), .pin9(1'b1), .pin10(1'b1), .pin11(_7420_1_pin2[0]), .pin12(_7420_1_pin4[2]),
    .pin13(_7420_1_pin4[1]), .pin14(_7420_1_pin4[0]), .pin15(_74161_1_pin15), .pin16(1'b1));
  _74161 _74161_2 (
    .pin1(_74161_1_pin1), .pin2(pxl), .pin3(1'b0), .pin4(1'b0), .pin5(1'b0), .pin6(1'b0),
    .pin7(_74161_1_pin15), .pin8(1'b0), .pin9(1'b1), .pin10(1'b1), .pin11(_7420_1_pin2[4]),
    .pin12(_7420_1_pin2[3]), .pin13(_7420_1_pin2[2]), .pin14(_7420_1_pin2[1]), .pin15(_74161_2_pin15),
    .pin16(1'b1));
  _74161 _74161_3 (
    .pin1(_74161_1_pin1), .pin2(pxl), .pin3(1'b0), .pin4(1'b0), .pin5(1'b0), .pin6(1'b0),
    .pin7(_74161_1_pin15), .pin8(1'b0), .pin9(1'b1), .pin10(_74161_2_pin15), .pin13(_7420_1_pin2[6]),
    .pin14(_7420_1_pin2[5]), .pin16(1'b1));  // open: pin11, pin12, pin15
  _7420 _7420_1 (
    .pin1(_7420_1_pin2[14]), .pin2(_7420_1_pin2[8]), .pin4(_7420_1_pin4[6]), .pin5(_7420_1_pin4[4]),
    .pin6(_7420_1_pin6), .pin7(1'b0), .pin8(_74161_1_pin1), .pin9(_7420_1_pin2[2]), .pin10(_7420_1_pin2[5]),
    .pin12(_7420_1_pin2[6]), .pin13(1'b1), .pin14(1'b1));  // open: pin3, pin11
  _74161 _74161_4 (
    .pin1(_7420_1_pin6), .pin2(_74161_1_pin1), .pin3(1'b0), .pin4(1'b0), .pin5(1'b0), .pin6(1'b0),
    .pin7(1'b1), .pin8(1'b0), .pin9(1'b1), .pin10(1'b1), .pin11(_7420_1_pin2[8]), .pin12(_7420_1_pin4[6]),
    .pin13(_7420_1_pin4[5]), .pin14(_7420_1_pin4[4]), .pin15(_74161_4_pin15), .pin16(1'b1));
  _74161 _74161_5 (
    .pin1(_7420_1_pin6), .pin2(_74161_1_pin1), .pin3(1'b0), .pin4(1'b0), .pin5(1'b0), .pin6(1'b0),
    .pin7(_74161_4_pin15), .pin8(1'b0), .pin9(1'b1), .pin10(1'b1), .pin11(_7420_1_pin2[12]),
    .pin12(_7420_1_pin2[11]), .pin13(_7420_1_pin2[10]), .pin14(_7420_1_pin2[9]), .pin15(_74161_5_pin15),
    .pin16(1'b1));
  _74161 _74161_6 (
    .pin1(_7420_1_pin6), .pin2(_74161_1_pin1), .pin3(1'b0), .pin4(1'b0), .pin5(1'b0), .pin6(1'b0),
    .pin7(_74161_4_pin15), .pin8(1'b0), .pin9(1'b1), .pin10(_74161_5_pin15), .pin13(_7420_1_pin2[14]),
    .pin14(_7420_1_pin2[13]), .pin16(1'b1));  // open: pin11, pin12, pin15
  ROM #(.AddrBits(16), .Bits(8)) charBuf (
    .A({1'b0, _7420_1_pin2[14:8], 1'b0, _7420_1_pin2[6:0]}), .sel(1'b1), .D(charBuf_d));
  ROM #(.AddrBits(16), .isProgramMemory("true"), .Bits(8)) charGen (
    .A({1'b0, charBuf_d, _7420_1_pin4[6:4], 1'b0, _7420_1_pin4[2:0]}), .sel(1'b1), .D(charGen_d));
  not not_1 (not_1_out, _7420_1_pin2[14]);
  _7400 _7400_1 (
    .pin1(1'b0), .pin2(1'b0), .pin4(_7400_1_pin4), .pin5(_7400_1_pin5), .pin6(_7400_1_pin6), .pin7(1'b0),
    .pin9(1'b1), .pin10(1'b1), .pin12(1'b1), .pin13(1'b1), .pin14(1'b1));  // open: pin3, pin8, pin11
  _7458 _7458_1 (
    .pin1(_7458_1_pin1), .pin2(1'b1), .pin3(_7458_1_pin3), .pin4(_7458_1_pin4), .pin5(_7458_1_pin5),
    .pin6(_7400_1_pin5), .pin7(1'b0), .pin8(_7458_1_pin8), .pin9(_7420_1_pin2[3]), .pin10(_7420_1_pin2[2]),
    .pin11(_7420_1_pin2[1]), .pin12(_7458_1_pin12), .pin13(_7458_1_pin13), .pin14(1'b1));
  _7404 _7404_1 (
    .pin1(_7420_1_pin2[4]), .pin2(_7458_1_pin5), .pin3(_7420_1_pin2[5]), .pin4(_7458_1_pin4),
    .pin5(_7420_1_pin2[6]), .pin6(_7458_1_pin3), .pin7(1'b0), .pin8(_7458_1_pin13), .pin9(_7420_1_pin2[1]),
    .pin10(_7458_1_pin12), .pin11(_7420_1_pin2[2]), .pin12(_7458_1_pin1), .pin13(_7420_1_pin2[3]),
    .pin14(1'b1));
  _744075 _744075_1 (
    .pin1(_7420_1_pin4[6]), .pin2(_7420_1_pin2[9]), .pin3(_744075_1_pin3), .pin4(_744075_1_pin4),
    .pin5(1'b0), .pin6(_744075_1_pin6), .pin7(1'b0), .pin8(_744075_1_pin8), .pin9(_744075_1_pin9),
    .pin10(_744075_1_pin10), .pin11(_744075_1_pin9), .pin12(_744075_1_pin6), .pin13(_744075_1_pin13),
    .pin14(1'b1));
  _7404 _7404_2 (
    .pin1(_7420_1_pin4[5]), .pin2(_744075_1_pin8), .pin3(_7420_1_pin2[8]), .pin4(_744075_1_pin4),
    .pin5(_7420_1_pin2[10]), .pin6(_744075_1_pin3), .pin7(1'b0), .pin8(_7404_2_pin8),
    .pin9(_7420_1_pin2[11]), .pin10(_7404_2_pin10), .pin11(_7420_1_pin2[12]), .pin12(_7404_2_pin12),
    .pin13(_7420_1_pin2[13]), .pin14(1'b1));
  _7458 _7458_2 (
    .pin1(not_1_out), .pin2(not_1_out), .pin3(_744075_1_pin3), .pin4(not_1_out), .pin5(_7404_2_pin8),
    .pin6(_7458_2_pin6), .pin7(1'b0), .pin8(_7458_2_pin8), .pin9(1'b1), .pin10(_7404_2_pin12),
    .pin11(not_1_out), .pin12(1'b1), .pin13(_7404_2_pin10), .pin14(1'b1));
  _744075 _744075_2 (
    .pin1(_7458_1_pin8), .pin2(_7458_1_pin5), .pin3(_7404_2_pin8), .pin4(_7404_2_pin10),
    .pin5(_7404_2_pin12), .pin6(_744075_1_pin13), .pin7(1'b0), .pin8(_7458_1_pin3), .pin9(_744075_2_pin9),
    .pin10(_7400_1_pin4), .pin11(1'b0), .pin12(_7458_2_pin8), .pin13(_7458_2_pin6), .pin14(1'b1));
  VGA vga_1 (
    .R(charGen_d[7:5]), .G(charGen_d[4:2]), .B({charGen_d[1:0], 1'b1}), .H(_744075_2_pin9),
    .V(_744075_1_pin10), .C(pxl));

  // Notes on the sheet:
  //   pxl: Hz: 2147483647
  //   Pulses on frame end
  //   Column counter
  //   Line counter
  //   cPixH
  //   Pixel coord
  //   bus
  //   cPixV
  //   cH
  //   cV
  //   contents of charBuf (hex, n*v repeats v):
  //   54,68,69,73,20,69,73,20,74,65,78,74,20,6d,6f,64,65,2e,20,53,65,65
  //   ,6d,73,20,74,6f,20,77,6f,72,6b,20,76,65,72,79,20,77,65,6c,6c,2e
  //   ,5*0,54,68,69,73,20,69,73,20,74,65,78,74,20,6d,6f,64,54,68,69
  //   ,73,20,69,73,20,74,65,78,74,20,6d,6f,64,176*0,54,68,69,73,20,69
  //   ,73,20,74,65,78,74,20,6d,6f,64
  //   contents of charGen (hex, n*v repeats v):
  //   18*0,ff,ff,12*0,5*ff,11*0,ff,ff,0,0,ff,ff,10*0,ff,ff,0,0,ff,ff
  //   ,10*0,6*ff,10*0,ff,ff,0,0,ff,ff,10*0,ff,ff,0,0,ff,ff
  //   !C
  //   !B
  //   !A
  //   !D
  //   !E
  //   !F
  //   High during hvis
  //   Low during hsync
  //   High during vvis
  //   Low during vsync
  //   low during frame runoff
  //   should be tied to write enable of buffer chips
  //   74hc244 is useful here
  //   frame runoff lasts just longer than 1ms
  //   during frame runoff:
  //   - put buffers in write mode
  //   - disconnect address/data buses from buffers
  //   - connect address/data buses to external device
  //   - probably good to use frame runoff going low as some kind of interrupt
  //   need 3 74hc244 per buffer chip (2 for address, 1 for data)
endmodule
